# Fritzing sketch demo_connection (saved by Fritzing 0.9.9b)
breadboards: 1

parts:
  Mod1 = Raspberry Pi 4B
  Part1 = SparkFun ESP8266 Thing
  R2 = Resistor [tolerance=±5% power=0.25 resistance=22k package=THT]
  U1 = POT [package=pot_mammoth]
  U2 = POT [package=pot_mammoth]
  U3 = POT [package=pot_mammoth]
  C1 = Capacitor Polarized [package=cpol-radial-10uf-25v]
  S1 = Pushbutton [package="[THT]"]
  S2 = Pushbutton [package="[THT]"]
  S3 = Pushbutton [package="[THT]"]
  R4 = Resistor [tolerance=±5% power=0.25 resistance=22k package=THT]
  R5 = Resistor [tolerance=±5% power=0.25 resistance=22k package=THT]
  S4 = H-Bridge with L298N
  M1 = DC Motor
  Part2 = ADS1115
  Part3 = SparkFun ESP8266 Thing

nets:
  3V3: Mod1.3V3, Mod1.5V, U1.S, U2.S, U3.S, C1.-, Part2.VDD
  N1: Mod1.GPIO2, Part2.SDA
  N2: Mod1.GPIO3, Part2.SCL
  GND: Mod1.GND, R2.Pin_0, U1.E, U2.E, U3.E, C1.+, S1.Pin_1, S1.Pin_2, S2.Pin_1, S2.Pin_2, S3.Pin_1, S3.Pin_2, R4.Pin_0, R5.Pin_0, Part2.GND
  N3: Mod1.GPIO14, Part1.U0RXI
  N4: Mod1.GPIO15, Part1.U0TXO
  N5: Mod1.GPIO25, R2.Pin_1, S1.Pin_3, S1.Pin_4
  N6: Mod1.GPIO8, S2.Pin_3, S2.Pin_4, R4.Pin_1
  N7: Mod1.GPIO7, S3.Pin_3, S3.Pin_4, R5.Pin_1
  N8: Mod1.ID_SD, Part3.U0TXO
  N9: Mod1.ID_SC, Part3.U0RXI
  N10: Mod1.GPIO12, S4.ENA
  N11: Mod1.GPIO16, S4.IN1
  N12: Mod1.GPIO20, S4.IN2
  N13: U1.A, Part2.A2
  N14: U2.A, Part2.A1
  N15: U3.A, Part2.A0
  N16: S4.M2-01, M1.pin_2
  N17: S4.M2-02, M1.pin_1

custom parts:
  H-Bridge with L298N: h-bridge
  ADS1115: ADC ADS1115
